// Logisim project dan_cpu.circ as structural Verilog: 1 circuit, main circuit cpu
module cpu (
  input  clk,
  input  [31:0] INSTRUCTION,
  input  [31:0] READ_DATA,
  output [31:0] WRITE_ADDRESS,
  output [31:0] PROGRAM_COUNTER,
  output [31:0] ra,
  output [31:0] sp,
  output [31:0] t0,
  output [31:0] t1,
  output [31:0] t2,
  output [31:0] s0,
  output [31:0] s1,
  output [31:0] a0,
  output [31:0] tohost,
  output [3:0] WRITE_ENABLE,
  output [31:0] WRITE_DATA
);

  wire ASel, BrEq, BrLt, BrUn, BSel, CSRSel, CSRWen, PCSel, RegWEn;
  wire [1:0] WBSel;
  wire [2:0] func3, ImmSel;
  wire [3:0] ALUSel;
  wire [6:0] func7;
  wire [24:0] IFrest;
  wire [31:0] adder_1_out, adder_2_out, extendedImm, multiplexer_1_out, multiplexer_2_out, multiplexer_3_out,
       multiplexer_4_out, multiplexer_5_out, readdata1, thisPC, writeData;

  Adder #(.width(32)) adder_1 (.a(PROGRAM_COUNTER), .b(32'h4), .out(adder_1_out));  // open: cin, cout
  Multiplexer #(.enable("false"), .width(32)) multiplexer_1 (
    .in0(adder_1_out), .in1(WRITE_ADDRESS), .out(multiplexer_1_out), .sel(PCSel));
  Register #(.width(32)) PC (.D(multiplexer_1_out), .clk(clk), .Q(PROGRAM_COUNTER));  // open: en, clr
  control_logic control_logic_1 (
    .CSRWen(CSRWen), .PCSel(PCSel), .RegWEn(RegWEn), .ImmSel(ImmSel), .BrUn(BrUn), .ASel(ASel), .BSel(BSel),
    .ALUSel(ALUSel), .MemRW(WRITE_ENABLE[3]), .WBSel(WBSel), .CSRSel(CSRSel),
    .inst({func7, IFrest[24:15], func3, IFrest[11:0]}), .BrEq(BrEq), .BrLt(BrLt));
  Register #(.width(32)) u_IFrest (
    .D(multiplexer_2_out), .clk(clk), .Q({func7, IFrest[24:15], func3, IFrest[11:0]}));  // open: en, clr
  Multiplexer #(.enable("false"), .width(32)) multiplexer_2 (
    .in0(INSTRUCTION), .in1(32'h13), .out(multiplexer_2_out), .sel(PCSel));
  Register #(.width(32)) register_1 (.D(PROGRAM_COUNTER), .clk(clk), .Q(thisPC));  // open: en, clr
  Multiplexer #(.enable("false"), .width(32)) multiplexer_3 (
    .in0(readdata1), .in1(extendedImm), .out(multiplexer_3_out), .sel(CSRSel));
  regfile regfile_1 (
    .rs1(IFrest[19:15]), .rs2(IFrest[24:20]), .rd(IFrest[11:7]), .Write_Data(writeData), .RegWEn(RegWEn),
    .clk(clk), .ra(ra), .sp(sp), .t0(t0), .t1(t1), .t2(t2), .s0(s0), .s1(s1), .a0(a0),
    .Read_Data_1(readdata1), .Read_Data_2(WRITE_DATA));
  csr csr_1 (.CSR_address(12'h51e), .CSR_din(multiplexer_3_out), .CSR_WE(CSRWen), .clk(clk), .tohost(tohost));
  branch_comp branch_comp_1 (.rs1(readdata1), .rs2(WRITE_DATA), .BrUn(BrUn), .BrEq(BrEq), .BrLt(BrLt));
  imm_gen imm_gen_1 (.inst({func7, IFrest[24:15], func3, IFrest[11:0]}), .ImmSel(ImmSel), .imm(extendedImm));
  Multiplexer #(.enable("false"), .width(32)) multiplexer_4 (
    .in0(readdata1), .in1(thisPC), .out(multiplexer_4_out), .sel(ASel));
  Multiplexer #(.enable("false"), .width(32)) multiplexer_5 (
    .in0(WRITE_DATA), .in1(extendedImm), .out(multiplexer_5_out), .sel(BSel));
  alu alu_1 (.Result(WRITE_ADDRESS), .A(multiplexer_4_out), .B(multiplexer_5_out), .ALUSel(ALUSel));
  Adder #(.width(32)) adder_2 (.a(32'h4), .b(thisPC), .out(adder_2_out));  // open: cin, cout
  Multiplexer #(.enable("false"), .select(2), .width(32)) multiplexer_6 (
    .in0(READ_DATA), .in1(WRITE_ADDRESS), .in2(adder_2_out), .out(writeData), .sel(WBSel));  // open: in3

  assign WRITE_ENABLE[2:0] = {3{WRITE_ENABLE[3]}};

  // Other names for the same wires on the sheet: ALUresult[31:0] = WRITE_ADDRESS; opcode[6:0] = IFrest[6:0];
  //   rd[4:0] = IFrest[11:7]; IFrest (some bits) = {func7, func3}; rs1[4:0] = IFrest[19:15]; rs2[4:0] = IFrest[24:20];
  //   readdata2[31:0] = WRITE_DATA; MemRW = WRITE_ENABLE[3]

  // Notes on the sheet:
  //   IF
  //   Output to IMEM
  //   IMEM (do **NOT** move this)
  //   Inputs from IMEM
  //   Inputs/Outputs for testing. Do **NOT** move these.
  //   ID
  //   Outputs To DMEM
  //   DMEM (do **NOT** move this)
  //   Inputs From DMEM
  //   EXE
endmodule
