// Logisim project control_logic.circ as structural Verilog: 1 circuit, main circuit control_logic
module control_logic (
  input  [31:0] inst,
  input  BrEq,
  input  BrLt,
  output PCSel,
  output RegWEn,
  output [2:0] ImmSel,
  output BrUn,
  output ASel,
  output BSel,
  output [3:0] ALUSel,
  output MemRW,
  output [1:0] WBSel,
  output CSRSel,
  output CSRWen
);

  wire and_13_out, and_14_out, and_15_out, and_16_out, and_18_out, and_19_out, and_21_out, and_22_out,
       inst2not, inst3not, inst4not, inst5not, inst6not, inst12not, inst13not, inst14not, inst25not,
       inst30not, isAdd, isAnd, isAuipc, isBeq, isBge, isBgeu, isBlt, isBltu, isBne, isCsrwtype, isIisAdd,
       isIisAnd, isIisOr, isIisSll, isIisSlt, isIisSra, isIisSrl, isIisXor, isImmtype, isItype, isJalr_out,
       isJalrtype, isLoadtype, isLui, isOr, isRisAdd, isRisAnd, isRisMul, isRisMulh, isRisMulhu, isRisOr,
       isRisSll, isRisSlt, isRisSra, isRisSrl, isRisSub, isRisXor, isRtype, isSBtype, isSll, isSlt, isSra,
       isSrl, isUJtype, isUtype, isXor, not_10_out, not_11_out, not_12_out, onlyRtype, or_2_out, or_3_out,
       or_18_out, WBALU, WBMem, WBPCplus4;
  wire [1:0] demultiplexer_21_out1, demultiplexer_22_out1, demultiplexer_23_out1;
  wire [2:0] immSelCsrw, immSelI, immSelR, immSelS, immSelSB, immSelU, immSelUJ;
  wire [3:0] or_17_out, SelAdd, SelAnd, SelB, SelMul, SelMulh, SelMulhu, SelOr, SelSll, SelSlt, SelSra,
       SelSrl, SelSub, SelXor;

  Demultiplexer #(.enable("false"), .width(3)) demultiplexer_1 (
    .out1(immSelI), .in(3'b000), .sel(isItype));  // open: out0
  Demultiplexer #(.enable("false"), .width(3)) demultiplexer_2 (
    .out1(immSelCsrw), .in(3'b101), .sel(isCsrwtype));  // open: out0
  and and_1 (isLoadtype, inst2not, inst3not, inst4not, inst5not, inst6not);
  and and_2 (isImmtype, inst2not, inst3not, inst[4], inst5not, inst6not);
  and and_3 (isJalrtype, inst[2], inst3not, inst4not, inst[5], inst[6]);
  and and_4 (isCsrwtype, inst2not, inst3not, inst[4], inst[5], inst[6]);
  and and_5 (isSBtype, inst2not, inst3not, inst4not, inst[5], inst[6]);
  not not_1 (inst2not, inst[2]);
  not not_2 (inst3not, inst[3]);
  not not_3 (inst4not, inst[4]);
  not not_4 (inst5not, inst[5]);
  not not_5 (inst6not, inst[6]);
  not not_6 (inst12not, inst[12]);
  not not_7 (inst13not, inst[13]);
  not not_8 (inst14not, inst[14]);
  not not_9 (inst30not, inst[30]);
  Demultiplexer #(.enable("false"), .width(3)) demultiplexer_3 (
    .out1(immSelS), .in(3'b001), .sel(MemRW));  // open: out0
  and and_6 (isBeq, inst12not, inst13not, inst14not);
  and and_7 (isBne, inst[12], inst13not, inst14not);
  and and_8 (isBlt, inst12not, inst13not, inst[14]);
  and and_9 (isBge, inst[12], inst13not, inst[14]);
  and and_10 (isBltu, inst12not, inst[13], inst[14]);
  and and_11 (isBgeu, inst[12], inst[13], inst[14]);
  or or_1 (isItype, isLoadtype, isImmtype, isJalrtype, isCsrwtype);
  Demultiplexer #(.enable("false"), .width(3)) demultiplexer_4 (
    .out1(immSelSB), .in(3'b010), .sel(isSBtype));  // open: out0
  and and_12 (BrUn, inst[13], isSBtype);
  not not_10 (not_10_out, BrLt);
  not not_11 (not_11_out, BrLt);
  Demultiplexer #(.enable("false"), .width(3)) demultiplexer_5 (
    .out1(immSelU), .in(3'b011), .sel(isUtype));  // open: out0
  not not_12 (not_12_out, BrEq);
  or or_2 (or_2_out, BrEq, not_10_out);
  or or_3 (or_3_out, BrEq, not_11_out);
  and and_13 (and_13_out, isBeq, isSBtype, BrEq);
  and and_14 (and_14_out, isBne, isSBtype, not_12_out);
  and and_15 (and_15_out, isBlt, isSBtype, BrLt);
  and and_16 (and_16_out, isBltu, isSBtype, BrLt);
  not not_13 (inst25not, inst[25]);
  and and_17 (MemRW, inst2not, inst3not, inst4not, inst[5], inst6not);
  Demultiplexer #(.enable("false"), .width(3)) demultiplexer_6 (
    .out1(immSelUJ), .in(3'b100), .sel(isUJtype));  // open: out0
  and and_18 (and_18_out, isBge, isSBtype, or_2_out);
  and and_19 (and_19_out, isBgeu, isSBtype, or_3_out);
  Demultiplexer #(.enable("false"), .width(3)) demultiplexer_7 (
    .out1(immSelR), .in(3'b110), .sel(isRtype));  // open: out0
  or or_4 (PCSel, and_13_out, and_14_out, and_15_out, and_18_out, and_16_out, and_19_out, isJalrtype, isUJtype);
  and and_20 (isSBtype, inst2not, inst3not, inst4not, inst[5], inst[6]);
  or or_5 (ASel, isSBtype, isUtype, isUJtype);
  not not_14 (BSel, isRtype);
  Demultiplexer #(.enable("false"), .width(4)) demultiplexer_8 (
    .out1(SelAdd), .in(4'b0000), .sel(isAdd));  // open: out0
  Demultiplexer #(.enable("false"), .width(4)) demultiplexer_9 (
    .out1(SelSub), .in(4'b1100), .sel(isRisSub));  // open: out0
  Demultiplexer #(.enable("false"), .width(4)) demultiplexer_10 (
    .out1(SelSll), .in(4'b0110), .sel(isSll));  // open: out0
  assign ImmSel = immSelI | immSelS | immSelSB | immSelCsrw | immSelU | immSelUJ | immSelR;  // OR_Gate or_6, 3 bits wide
  and and_21 (and_21_out, inst[2], inst3not, inst[4], inst5not, inst6not);
  and and_22 (and_22_out, inst[2], inst3not, inst[4], inst[5], inst6not);
  or or_7 (isAdd, isRisAdd, isIisAdd);
  or or_8 (isSll, isRisSll, isIisSll);
  or or_9 (isSlt, isIisSlt, isRisSlt);
  or or_10 (isUtype, and_21_out, and_22_out);
  and and_23 (isRisAdd, inst12not, inst13not, inst14not, inst30not, isRtype);
  and and_24 (isRisSub, inst12not, inst13not, inst14not, inst[30], isRtype);
  and and_25 (isRisSll, inst[12], inst13not, inst14not, inst30not, isRtype);
  and and_26 (isIisAdd, inst12not, inst13not, inst14not, isImmtype);
  and and_27 (isIisSll, inst[12], inst13not, inst14not, inst30not, isImmtype);
  and and_28 (isIisSlt, inst12not, inst[13], inst14not, isImmtype);
  Demultiplexer #(.enable("false"), .width(4)) demultiplexer_11 (
    .out1(SelSlt), .in(4'b0111), .sel(isSlt));  // open: out0
  Demultiplexer #(.enable("false"), .width(4)) demultiplexer_12 (
    .out1(SelXor), .in(4'b0011), .sel(isXor));  // open: out0
  Demultiplexer #(.enable("false"), .width(4)) demultiplexer_13 (
    .out1(SelSrl), .in(4'b0100), .sel(isSrl));  // open: out0
  or or_11 (isXor, isIisXor, isRisXor);
  or or_12 (isSrl, isIisSrl, isRisSrl);
  or or_13 (isSra, isIisSra, isRisSra);
  Demultiplexer #(.enable("false"), .width(4)) demultiplexer_14 (
    .out1(SelSra), .in(4'b0101), .sel(isSra));  // open: out0
  Demultiplexer #(.enable("false"), .width(4)) demultiplexer_15 (.out1(SelOr), .in(4'b0010), .sel(isOr));  // open: out0
  Demultiplexer #(.enable("false"), .width(4)) demultiplexer_16 (
    .out1(SelAnd), .in(4'b0001), .sel(isAnd));  // open: out0
  and and_29 (isUJtype, inst[2], inst[3], inst4not, inst[5], inst[6]);
  and and_30 (isRisSlt, inst12not, inst[13], inst14not, inst30not, isRtype);
  and and_31 (isRisXor, inst12not, inst13not, inst[14], inst30not, isRtype);
  and and_32 (isRisSrl, inst[12], inst13not, inst[14], inst30not, isRtype);
  and and_33 (isIisXor, inst12not, inst13not, inst[14], isImmtype);
  and and_34 (isIisSrl, inst[12], inst13not, inst[14], inst30not, isImmtype);
  and and_35 (isIisSra, inst[12], inst13not, inst[14], inst[30], isImmtype);
  or or_14 (isOr, isIisOr, isRisOr);
  or or_15 (isAnd, isIisAnd, isRisAnd);
  Demultiplexer #(.enable("false"), .width(4)) demultiplexer_17 (
    .out1(SelMul), .in(4'b1010), .sel(isRisMul));  // open: out0
  Demultiplexer #(.enable("false"), .width(4)) demultiplexer_18 (
    .out1(SelMulh), .in(4'b1110), .sel(isRisMulh));  // open: out0
  Demultiplexer #(.enable("false"), .width(4)) demultiplexer_19 (
    .out1(SelMulhu), .in(4'b1011), .sel(isRisMulhu));  // open: out0
  Demultiplexer #(.enable("false"), .width(4)) demultiplexer_20 (.out1(SelB), .in(4'b1101), .sel(isLui));  // open: out0
  and and_36 (isRisSra, inst[12], inst13not, inst[14], inst[30], isRtype);
  and and_37 (isRisOr, inst12not, inst[13], inst[14], inst30not, isRtype);
  and and_38 (isRisAnd, inst[12], inst[13], inst[14], inst30not, isRtype);
  and and_39 (isIisOr, inst12not, inst[13], inst[14], isImmtype);
  and and_40 (isIisAnd, inst[12], inst[13], inst[14], isImmtype);
  and and_41 (isRtype, inst2not, inst3not, inst[4], inst[5], inst6not);
  or or_16 (RegWEn, isRtype, isItype, isUtype, isUJtype);
  and and_42 (isRisMul, inst12not, inst13not, inst14not, inst[25], isRtype);
  and and_43 (isRisMulh, inst[12], inst13not, inst14not, inst[25], isRtype);
  and and_44 (isRisMulhu, inst[12], inst[13], inst14not, inst[25], isRtype);
  Demultiplexer #(.enable("false"), .width(2)) demultiplexer_21 (
    .out1(demultiplexer_21_out1), .in(2'b00), .sel(WBMem));  // open: out0
  Demultiplexer #(.enable("false"), .width(2)) demultiplexer_22 (
    .out1(demultiplexer_22_out1), .in(2'b01), .sel(WBALU));  // open: out0
  Demultiplexer #(.enable("false"), .width(2)) demultiplexer_23 (
    .out1(demultiplexer_23_out1), .in(2'b10), .sel(WBPCplus4));  // open: out0
  assign or_17_out = SelAdd | SelSub | SelSll | SelSlt | SelXor | SelSrl | SelB | SelSra | SelOr | SelAnd | SelMul | SelMulh | SelMulhu;  // OR_Gate or_17, 4 bits wide
  xnor xnor_1 (WBALU, WBMem, WBPCplus4);
  or or_18 (or_18_out, isRtype, isLui, isItype);
  not not_15 (onlyRtype, or_18_out);
  Multiplexer #(.enable("false"), .width(4)) multiplexer_1 (
    .in0(or_17_out), .in1(4'b0000), .out(ALUSel), .sel(onlyRtype));
  and isLw (WBMem, inst2not, inst3not, inst4not, inst5not, inst6not);
  and isJalr (isJalr_out, inst[2], inst3not, inst4not, inst[5], inst[6]);
  or or_19 (WBPCplus4, isJalr_out, isUJtype);
  assign WBSel = demultiplexer_21_out1 | demultiplexer_22_out1 | demultiplexer_23_out1;  // OR_Gate or_20, 2 bits wide
  and and_45 (isLui, inst[2], inst3not, inst[4], inst[5], inst6not);
  and and_46 (isAuipc, inst[2], inst3not, inst[4], inst5not, inst6not);

  assign CSRSel = inst[14];
  assign CSRWen = 1'b1;

  // Other names for the same wires on the sheet: isStype = MemRW

  // Notes on the sheet:
  //   INPUTS to your circuit
  //   opcode[6:2]
  //   func3
  //   func7[5]
  //   done
  //   done
  //   done
  //   BrUn
  //   DON'T CHANGE THE LOCATIONS OF THE INPUTS AND OUTPUTS!
  //   OUTPUT from your circuit
  //   done
  //   done
  //   done
  //   done
  //   PCSel
  //   done
  //   done
  //   ImmSel
  //   CSR
  //   ASel&BSel
  //   MemRW
  //   ALUSel
  //   RegWEn
  //   WBSel
endmodule
