// Logisim project cpu.circ as structural Verilog: 1 circuit, main circuit cpu
module cpu (
  input  clk,
  input  [31:0] INSTRUCTION,
  input  [31:0] READ_DATA,
  output [31:0] WRITE_ADDRESS,
  output [31:0] PROGRAM_COUNTER,
  output [31:0] ra,
  output [31:0] sp,
  output [31:0] t0,
  output [31:0] t1,
  output [31:0] t2,
  output [31:0] s0,
  output [31:0] s1,
  output [31:0] a0,
  output [31:0] tohost,
  output [3:0] WRITE_ENABLE,
  output [31:0] WRITE_DATA
);

  wire ASel, BrEq, BrLt, BrUn, BSel, CSRSel, CSRWen, PCSel, RegWEn;
  wire [1:0] WBSel;
  wire [2:0] ImmSel;
  wire [3:0] ALUSel;
  wire [31:0] adder_1_out, imm, INSTRUCTION_2, multiplexer_1_out, multiplexer_2_out, multiplexer_4_out,
       multiplexer_5_out, multiplexer_6_out, PC_plus_4, PROGRAM_COUNTER_2, Read_Data_1, Write_data_t;

  Multiplexer #(.enable("false"), .width(32)) multiplexer_1 (
    .in0(INSTRUCTION), .in1(32'h13), .out(multiplexer_1_out), .sel(PCSel));
  Multiplexer #(.enable("false"), .width(32)) multiplexer_2 (
    .in0(PC_plus_4), .in1(WRITE_ADDRESS), .out(multiplexer_2_out), .sel(PCSel));
  Register #(.width(32)) PC (.D(multiplexer_2_out), .clk(clk), .Q(PROGRAM_COUNTER));  // open: en, clr
  Adder #(.width(32)) adder_1 (.a(PROGRAM_COUNTER_2), .b(32'h4), .out(adder_1_out));  // open: cin, cout
  Register #(.width(32)) register_1 (.D(multiplexer_1_out), .clk(clk), .Q(INSTRUCTION_2));  // open: en, clr
  Register #(.width(32)) register_2 (.D(PROGRAM_COUNTER), .clk(clk), .Q(PROGRAM_COUNTER_2));  // open: en, clr
  Adder #(.width(32)) adder_2 (.a(PROGRAM_COUNTER), .b(32'h4), .out(PC_plus_4));  // open: cin, cout
  Multiplexer #(.enable("false"), .select(2), .width(32)) multiplexer_3 (
    .in0(READ_DATA), .in1(WRITE_ADDRESS), .in2(adder_1_out), .out(Write_data_t), .sel(WBSel));  // open: in3
  Multiplexer #(.enable("false"), .width(32)) multiplexer_4 (
    .in0(Read_Data_1), .in1(imm), .out(multiplexer_4_out), .sel(CSRSel));
  csr csr_1 (.CSR_address(12'h51e), .CSR_din(multiplexer_4_out), .CSR_WE(CSRWen), .clk(clk), .tohost(tohost));
  regfile regfile_1 (
    .rs1(INSTRUCTION_2[19:15]), .rs2(INSTRUCTION_2[24:20]), .rd(INSTRUCTION_2[11:7]),
    .Write_Data(Write_data_t), .RegWEn(RegWEn), .clk(clk), .ra(ra), .sp(sp), .t0(t0), .t1(t1), .t2(t2),
    .s0(s0), .s1(s1), .a0(a0), .Read_Data_1(Read_Data_1), .Read_Data_2(WRITE_DATA));
  Multiplexer #(.enable("false"), .width(32)) multiplexer_5 (
    .in0(Read_Data_1), .in1(PROGRAM_COUNTER_2), .out(multiplexer_5_out), .sel(ASel));
  Multiplexer #(.enable("false"), .width(32)) multiplexer_6 (
    .in0(WRITE_DATA), .in1(imm), .out(multiplexer_6_out), .sel(BSel));
  control_logic control_logic_1 (
    .CSRWen(CSRWen), .PCSel(PCSel), .RegWEn(RegWEn), .ImmSel(ImmSel), .BrUn(BrUn), .ASel(ASel), .BSel(BSel),
    .ALUSel(ALUSel), .MemRW(WRITE_ENABLE[3]), .WBSel(WBSel), .CSRSel(CSRSel), .inst(INSTRUCTION_2),
    .BrEq(BrEq), .BrLt(BrLt));
  alu alu_1 (.Result(WRITE_ADDRESS), .A(multiplexer_5_out), .B(multiplexer_6_out), .ALUSel(ALUSel));
  imm_gen imm_gen_1 (.inst(INSTRUCTION_2), .ImmSel(ImmSel), .imm(imm));
  branch_comp branch_comp_1 (.rs1(Read_Data_1), .rs2(WRITE_DATA), .BrUn(BrUn), .BrEq(BrEq), .BrLt(BrLt));

  assign WRITE_ENABLE[2:0] = {3{WRITE_ENABLE[3]}};

  // Other names for the same wires on the sheet: ALU_output[31:0] = WRITE_ADDRESS; rd[4:0] = INSTRUCTION_2[11:7];
  //   rs1[4:0] = INSTRUCTION_2[19:15]; rs2[4:0] = INSTRUCTION_2[24:20]; Read_Data_2[31:0] = WRITE_DATA;
  //   MemRW = WRITE_ENABLE[3]

  // Notes on the sheet:
  //   Output to IMEM
  //   IMEM (do **NOT** move this)
  //   Inputs from IMEM
  //   It is OK to move the PC, RegFile, ALU, MEM, Branch Comp, Imm Gen, and Control Logic to wherever is most convenient for you when constructing your CPU, and to delete this text
  //   Inputs/Outputs for testing. Do **NOT** move these.
  //   Outputs To DMEM
  //   DMEM (do **NOT** move this)
  //   Inputs From DMEM
endmodule
